# Fritzing sketch doorbell_flasher (saved by Fritzing 0.9.3b)
circuit board: 6cm x 6cm
breadboards: 1

parts:
  R1 = Resistor [tolerance=±5% resistance=68 package=THT]
  LED1 = LED - 5mm [color="Red (633nm)" package="5 mm [THT]"]
  LED2 = LED - 5mm [color="Red (633nm)" package="5 mm [THT]"]
  LED3 = LED - 5mm [color="Red (633nm)" package="5 mm [THT]"]
  LED4 = LED - 5mm [color="Red (633nm)" package="5 mm [THT]"]
  LED6 = LED - 5mm [color="Red (633nm)" package="5 mm [THT]"]
  LED7 = LED - 5mm [color="Red (633nm)" package="5 mm [THT]"]
  LED8 = LED - 5mm [color="Red (633nm)" package="5 mm [THT]"]
  ESP8266 = Adafruit Feather HUZZAH ESP8266 [part_number="Adafruit #2821"]
  ON/OFF = SPST Switch [package=switch-spdt]
  RGB = RGB LED (com. cathode, rgb) [package="5 mm [THT]"]
  LED5 = LED - 5mm [color="Red (633nm)" package="5 mm [THT]"]
  Mosfet = MOSFET-NCHANNEL [package=to220v]
  R2 = Resistor [tolerance=±5% resistance=220 package="1206 [SMD]"]
  R3 = Resistor [tolerance=±5% resistance=220 package="1206 [SMD]"]
  R4 = Resistor [tolerance=±5% resistance=220 package="1206 [SMD]"]
  VBR = Round Pushbutton

nets:
  N1: R1.Pin_0, Mosfet.G
  N2: R1.Pin_1, ESP8266.GND, ON/OFF.O, RGB.common_cathode
  N3: LED1.cathode, LED2.cathode, LED3.cathode, LED4.cathode, LED6.cathode, LED7.cathode, LED8.cathode, LED5.cathode, Mosfet.D, VBR.leg1
  N4: LED1.anode, LED2.anode, LED3.anode, LED4.anode, LED6.anode, LED7.anode, LED8.anode, ESP8266.VBAT, LED5.anode, VBR.leg0
  N5: ESP8266.GPIO14/SCK, Mosfet.S
  N6: ESP8266.EN, ON/OFF.P
  N7: ESP8266.GPIO16, R2.Pin_0
  N8: ESP8266.GPIO2, R3.Pin_0
  N9: ESP8266.GPIO5/SCL, R4.Pin_0
  N10: RGB.red_anode, R4.Pin_1
  N11: RGB.green_anode, R3.Pin_1
  N12: RGB.blue_anode, R2.Pin_1

custom parts:
  Adafruit Feather HUZZAH ESP8266: his is the Adafruit Feather HUZZAH ESP8266 - our take on an 'all-in-one' ESP8266 WiFi development board with built in USB and battery charging. Its an ESP8266 WiFi module with all the extras you need, ready to rock! We have other boards in the Feather family, check'em out here. At the Feather HUZZAH's heart is an ESP8266 WiFi microcontroller clocked at 80 MHz and at 3.3V logic. This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
